// Logisim project Project1Given.circ as structural Verilog: 4 circuits, main circuit main
module main (
  input  in_1,
  input  in_2,
  input  in_3,
  input  in_4,
  input  Five,
  output N,
  output E,
  output [3:0] out_8
);

  wire fiveseven_1_a, fiveseven_1_b, fiveseven_1_c, fiveseven_1_d, fiveseven_1_e, fiveseven_1_f,
       fiveseven_1_g;

  Compare compare_1 (.X0(1'b1), .X1(1'b0), .X2(1'b1), .Y0(1'b1), .Y1(1'b1), .Y2(1'b1), .N(N), .E(E));
  Gray gray_1 (.B0(1'b1), .B1(1'b0), .B2(1'b1), .B3(1'b1), .G0(out_8[0]), .G1(out_8[1]), .G2(out_8[2]), .G3(out_8[3]));
  FiveSeven fiveseven_1 (
    .V(in_1), .W(in_2), .X(in_3), .Y(in_4), .Z(Five), .A(fiveseven_1_a), .B(fiveseven_1_b),
    .C(fiveseven_1_c), .D(fiveseven_1_d), .E(fiveseven_1_e), .F(fiveseven_1_f), .G(fiveseven_1_g));
  _7_Segment_Display u_7_segment_display_1 (
    .g(fiveseven_1_g), .f(fiveseven_1_f), .a(fiveseven_1_a), .b(fiveseven_1_b), .e(fiveseven_1_e),
    .d(fiveseven_1_d), .c(fiveseven_1_c));  // open: dp
endmodule

module Compare (
  input  X0,
  input  X1,
  input  X2,
  input  Y0,
  input  Y1,
  input  Y2,
  output N,
  output E
);

  wire and_1_out, and_2_out, and_3_out, and_4_out, and_5_out, and_6_out, not_1_out, not_2_out, not_3_out,
       xnor_1_out, xnor_2_out, xnor_3_out;

  not not_1 (not_1_out, X1);
  not not_2 (not_2_out, X2);
  not not_3 (not_3_out, X0);
  and and_1 (and_1_out, not_1_out, Y1);
  and and_2 (and_2_out, not_2_out, Y2);
  xnor xnor_1 (xnor_1_out, X0, Y0);
  xnor xnor_2 (xnor_2_out, X1, Y1);
  xnor xnor_3 (xnor_3_out, X2, Y2);
  and and_3 (and_3_out, not_3_out, Y0);
  and and_4 (and_4_out, and_1_out, xnor_3_out);
  and and_5 (and_5_out, xnor_3_out, xnor_2_out);
  and and_6 (and_6_out, and_3_out, and_5_out);
  and and_7 (E, xnor_1_out, xnor_2_out, xnor_3_out);
  or or_1 (N, and_4_out, and_2_out, and_6_out);
endmodule

module Gray (
  input  B0,
  input  B1,
  input  B2,
  input  B3,
  output G0,
  output G1,
  output G2,
  output G3
);

  wire and_1_out, and_2_out, and_3_out, and_4_out, and_5_out, and_6_out, and_7_out, and_8_out, and_9_out,
       and_10_out, and_11_out, not_2_out, not_3_out, not_4_out, not_5_out, not_6_out, not_7_out, not_8_out,
       not_9_out, not_10_out, not_11_out, not_12_out;

  // NOT_Gate not_1 has open pins: in=B3, out=open
  not not_2 (not_2_out, B2);
  not not_3 (not_3_out, B1);
  not not_4 (not_4_out, B0);
  and and_1 (and_1_out, B2, not_3_out);
  and and_2 (and_2_out, B2, not_4_out);
  and and_3 (and_3_out, not_2_out, B1, B0);
  or or_1 (G2, and_1_out, and_2_out, and_3_out);
  not not_5 (not_5_out, B3);
  not not_6 (not_6_out, B2);
  not not_7 (not_7_out, B1);
  not not_8 (not_8_out, B0);
  not not_9 (not_9_out, B3);
  not not_10 (not_10_out, B2);
  not not_11 (not_11_out, B1);
  not not_12 (not_12_out, B0);
  and and_4 (and_4_out, not_5_out, B0);
  and and_5 (and_5_out, not_5_out, B1);
  and and_6 (and_6_out, not_5_out, B2);
  and and_7 (and_7_out, B3, not_6_out, not_7_out, not_8_out);
  and and_8 (and_8_out, not_9_out, not_10_out);
  and and_9 (and_9_out, not_9_out, not_12_out, not_11_out);
  and and_10 (and_10_out, B3, B2, B0);
  and and_11 (and_11_out, B3, B2, B1);
  or or_2 (G0, and_4_out, and_5_out, and_6_out, and_7_out);
  or or_3 (G1, and_8_out, and_9_out, and_10_out, and_11_out);

  assign G3 = B1;

  // Other names for the same wires on the sheet: B0_t = B3; B1_t = B2; B3_t = B0; B2_t = B1; G0_t = B1; G1_t = G2;
  //   G2_t = G1; G3_t = G0
endmodule

module FiveSeven (
  input  V,
  input  W,
  input  X,
  input  Y,
  input  Z,
  output A,
  output B,
  output C,
  output D,
  output E,
  output F,
  output G
);

  wire and_1_out, and_2_out, and_3_out, and_4_out, and_5_out, and_6_out, and_7_out, and_8_out, and_9_out,
       and_10_out, and_11_out, and_12_out, and_13_out, and_14_out, and_15_out, and_16_out, and_17_out,
       not_1_out, not_2_out, not_3_out, not_4_out, not_8_out, not_9_out, not_10_out, not_11_out, not_12_out;

  not not_1 (not_1_out, V);
  not not_2 (not_2_out, W);
  not not_3 (not_3_out, X);
  not not_4 (not_4_out, Y);
  // NOT_Gate not_5 has open pins: in=Z, out=open
  // NOT_Gate not_6 has open pins: in=V, out=open
  // NOT_Gate not_7 has open pins: in=W, out=open
  and and_1 (and_1_out, Z, not_2_out);
  and and_2 (and_2_out, Z, not_3_out);
  and and_3 (and_3_out, V, Z);
  and and_4 (and_4_out, W, Y, not_3_out);
  and and_5 (and_5_out, W, X, not_4_out);
  and and_6 (and_6_out, V, not_2_out, Y);
  and and_7 (and_7_out, V, not_2_out, X);
  and and_8 (and_8_out, V, W, X);
  and and_9 (and_9_out, not_1_out, X, Y);
  or or_1 (A, and_1_out, and_2_out, and_3_out, and_4_out, and_5_out, and_6_out, and_7_out, and_8_out, and_9_out);
  not not_8 (not_8_out, V);
  not not_9 (not_9_out, W);
  not not_10 (not_10_out, X);
  not not_11 (not_11_out, Y);
  not not_12 (not_12_out, Z);
  and and_10 (and_10_out, X, Y);
  and and_11 (and_11_out, W, Y);
  and and_12 (and_12_out, W, X);
  and and_13 (and_13_out, V, Z);
  and and_14 (and_14_out, not_8_out, Y, not_12_out);
  and and_15 (and_15_out, not_8_out, X, not_12_out);
  and and_16 (and_16_out, not_8_out, W, not_12_out);
  and and_17 (and_17_out, V, not_9_out, not_10_out, not_11_out);
  or or_2 (B, and_10_out, and_11_out, and_12_out, and_13_out, and_14_out, and_15_out, and_16_out, and_17_out);

  // Other names for the same wires on the sheet: a_t = V; b_t = W; c_t_t = X; d_t_t = Y; e_t_t = Z
endmodule
